// Logisim project main.circ as structural Verilog
module main (
);

  TTY tty_1 ();  // open: data, clk, we, clr
  DotMatrix #(.inputtype("row"), .matrixcols(32), .matrixrows(32)) dotmatrix_1 ();  // open: row0, row1, row2, row3, row4, row5, row6, row7, row8, row9, row10, row11, row12, row13, row14, row15, row16, row17, row18, row19, row20, row21, row22, row23, row24, row25, row26, row27, row28, row29, row30, row31
endmodule

module \cell  (
  input  [7:0] around,
  input  [7:0] born_rule,
  input  [7:0] survival_rule,
  input  clock,
  input  out,
  input  reset,
  output state
);

  wire and_1_out, check_rules_1_born, check_rules_1_survive, or_1_out;
  wire [3:0] bitadder_1_out;

  BitAdder bitadder_1 (.in0(around), .out(bitadder_1_out));
  check_rules check_rules_1 (
    .count(bitadder_1_out), .born_rule(born_rule), .survival_rule(survival_rule), .Born(check_rules_1_born),
    .survive(check_rules_1_survive));
  D_Flip_Flop d_ff_1 (.clk(clock), .D(or_1_out), .Q(state), .preset(out), .reset(reset));  // open: Qn, en
  and and_1 (and_1_out, check_rules_1_survive, state);
  or or_1 (or_1_out, check_rules_1_born, and_1_out);
endmodule

module line (
  input  [7:0] survival_rules,
  input  [7:0] born_rules,
  input  clock,
  input  reset,
  input  [2:0] left_cells,
  input  [2:0] right_cells,
  input  [31:0] up,
  input  [31:0] out_force,
  input  [31:0] down,
  output [31:0] output_up,
  output [31:0] output_down
);

  wire _22;

  \cell  cell_1 (
    .around({up[0], up[1], down[0], down[1], left_cells[0], left_cells[1], left_cells[2], output_down[1]}),
    .born_rule(born_rules), .survival_rule(survival_rules), .clock(clock), .out(out_force[0]), .reset(reset),
    .state(output_down[0]));
  \cell  cell_2 (
    .around({up[7], down[7], up[8], down[8], up[9], down[9], output_down[7], output_down[9]}),
    .born_rule(born_rules), .survival_rule(survival_rules), .clock(clock), .out(out_force[8]), .reset(reset),
    .state(output_down[8]));
  \cell  cell_3 (
    .around({up[15], down[15], up[16], down[16], up[17], down[17], output_down[15], output_down[17]}),
    .born_rule(born_rules), .survival_rule(survival_rules), .clock(clock), .out(out_force[16]),
    .reset(reset), .state(output_down[16]));
  \cell  cell_4 (
    .around({up[23], down[23], up[24], down[24], up[25], down[25], output_down[23], output_down[25]}),
    .born_rule(born_rules), .survival_rule(survival_rules), .clock(clock), .out(out_force[24]),
    .reset(reset), .state(output_down[24]));
  \cell  cell_5 (
    .around({up[0], down[0], up[1], down[1], up[2], down[2], output_down[0], output_down[2]}),
    .born_rule(born_rules), .survival_rule(survival_rules), .clock(clock), .out(out_force[1]), .reset(reset),
    .state(output_down[1]));
  \cell  cell_6 (
    .around({up[8], down[8], up[9], down[9], up[10], down[10], output_down[8], output_down[10]}),
    .born_rule(born_rules), .survival_rule(survival_rules), .clock(clock), .out(out_force[9]), .reset(reset),
    .state(output_down[9]));
  \cell  cell_7 (
    .around({up[16], down[16], up[17], down[17], up[18], down[18], output_down[16], output_down[18]}),
    .born_rule(born_rules), .survival_rule(survival_rules), .clock(clock), .out(out_force[17]),
    .reset(reset), .state(output_down[17]));
  \cell  cell_8 (
    .around({up[24], down[24], up[25], down[25], up[26], down[26], output_down[24], output_down[26]}),
    .born_rule(born_rules), .survival_rule(survival_rules), .clock(clock), .out(out_force[25]),
    .reset(reset), .state(output_down[25]));
  \cell  cell_9 (
    .around({up[1], down[1], up[2], down[2], up[3], down[3], output_down[1], output_down[3]}),
    .born_rule(born_rules), .survival_rule(survival_rules), .clock(clock), .out(out_force[2]), .reset(reset),
    .state(output_down[2]));
  \cell  cell_10 (
    .around({up[9], down[9], up[10], down[10], up[11], down[11], output_down[9], output_down[11]}),
    .born_rule(born_rules), .survival_rule(survival_rules), .clock(clock), .out(out_force[10]),
    .reset(reset), .state(output_down[10]));
  \cell  cell_11 (
    .around({up[17], down[17], up[18], down[18], up[19], down[19], output_down[17], output_down[19]}),
    .born_rule(born_rules), .survival_rule(survival_rules), .clock(clock), .out(out_force[18]),
    .reset(reset), .state(output_down[18]));
  \cell  cell_12 (
    .around({up[25], down[25], up[26], down[26], up[27], down[27], output_down[25], output_down[27]}),
    .born_rule(born_rules), .survival_rule(survival_rules), .clock(clock), .out(out_force[26]),
    .reset(reset), .state(output_down[26]));
  \cell  cell_13 (
    .around({up[2], down[2], up[3], down[3], up[4], down[4], output_down[2], output_down[4]}),
    .born_rule(born_rules), .survival_rule(survival_rules), .clock(clock), .out(out_force[3]), .reset(reset),
    .state(output_down[3]));
  \cell  cell_14 (
    .around({up[10], down[10], up[11], down[11], up[12], down[12], output_down[10], output_down[12]}),
    .born_rule(born_rules), .survival_rule(survival_rules), .clock(clock), .out(out_force[11]),
    .reset(reset), .state(output_down[11]));
  \cell  cell_15 (
    .around({up[18], down[18], up[19], down[19], up[20], down[20], output_down[18], output_down[20]}),
    .born_rule(born_rules), .survival_rule(survival_rules), .clock(clock), .out(out_force[19]),
    .reset(reset), .state(output_down[19]));
  \cell  cell_16 (
    .around({up[26], down[26], up[27], down[27], up[28], down[28], output_down[26], output_down[28]}),
    .born_rule(born_rules), .survival_rule(survival_rules), .clock(clock), .out(out_force[27]),
    .reset(reset), .state(output_down[27]));
  \cell  cell_17 (
    .around({up[3], down[3], up[4], down[4], up[5], down[5], output_down[3], output_down[5]}),
    .born_rule(born_rules), .survival_rule(survival_rules), .clock(clock), .out(out_force[4]), .reset(reset),
    .state(output_down[4]));
  \cell  cell_18 (
    .around({up[11], down[11], up[12], down[12], up[13], down[13], output_down[11], output_down[13]}),
    .born_rule(born_rules), .survival_rule(survival_rules), .clock(clock), .out(out_force[12]),
    .reset(reset), .state(output_down[12]));
  \cell  cell_19 (
    .around({up[19], down[19], up[20], down[20], up[21], down[21], output_down[19], output_down[21]}),
    .born_rule(born_rules), .survival_rule(survival_rules), .clock(clock), .out(out_force[20]),
    .reset(reset), .state(output_down[20]));
  \cell  cell_20 (
    .around({up[27], down[27], up[28], down[28], up[29], down[29], output_down[27], output_down[29]}),
    .born_rule(born_rules), .survival_rule(survival_rules), .clock(clock), .out(out_force[28]),
    .reset(reset), .state(output_down[28]));
  \cell  cell_21 (
    .around({up[4], down[4], up[5], down[5], up[6], down[6], output_down[4], output_down[6]}),
    .born_rule(born_rules), .survival_rule(survival_rules), .clock(clock), .out(out_force[5]), .reset(reset),
    .state(output_down[5]));
  \cell  cell_22 (
    .around({up[12], down[12], up[13], down[13], up[14], down[14], output_down[12], output_down[14]}),
    .born_rule(born_rules), .survival_rule(survival_rules), .clock(clock), .out(out_force[13]),
    .reset(reset), .state(output_down[13]));
  \cell  cell_23 (
    .around({up[20], down[20], up[21], down[21], up[22], down[22], output_down[20], output_down[22]}),
    .born_rule(born_rules), .survival_rule(survival_rules), .clock(clock), .out(out_force[21]),
    .reset(reset), .state(output_down[21]));
  \cell  cell_24 (
    .around({up[28], down[28], up[29], down[29], up[30], down[30], output_down[28], output_down[30]}),
    .born_rule(born_rules), .survival_rule(survival_rules), .clock(clock), .out(out_force[29]),
    .reset(reset), .state(output_down[29]));
  \cell  cell_25 (
    .around({up[5], down[5], up[6], down[6], up[7], down[7], output_down[5], output_down[7]}),
    .born_rule(born_rules), .survival_rule(survival_rules), .clock(clock), .out(out_force[6]), .reset(reset),
    .state(output_down[6]));
  \cell  cell_26 (
    .around({up[13], down[13], up[14], down[14], up[15], down[15], output_down[13], output_down[15]}),
    .born_rule(born_rules), .survival_rule(survival_rules), .clock(clock), .out(out_force[14]),
    .reset(reset), .state(output_down[14]));
  \cell  cell_27 (
    .around({up[21], down[21], up[22], down[22], up[23], down[23], output_down[21], output_down[23]}),
    .born_rule(born_rules), .survival_rule(survival_rules), .clock(clock), .out(_22), .reset(reset),
    .state(output_down[22]));
  \cell  cell_28 (
    .around({up[29], down[29], up[30], down[30], up[31], down[31], output_down[29], output_down[31]}),
    .born_rule(born_rules), .survival_rule(survival_rules), .clock(clock), .out(out_force[30]),
    .reset(reset), .state(output_down[30]));
  \cell  cell_29 (
    .around({up[6], down[6], up[7], down[7], up[8], down[8], output_down[6], output_down[8]}),
    .born_rule(born_rules), .survival_rule(survival_rules), .clock(clock), .out(out_force[7]), .reset(reset),
    .state(output_down[7]));
  \cell  cell_30 (
    .around({up[14], down[14], up[15], down[15], up[16], down[16], output_down[14], output_down[16]}),
    .born_rule(born_rules), .survival_rule(survival_rules), .clock(clock), .out(out_force[15]),
    .reset(reset), .state(output_down[15]));
  \cell  cell_31 (
    .around({up[22], down[22], up[23], down[23], up[24], down[24], output_down[22], output_down[24]}),
    .born_rule(born_rules), .survival_rule(survival_rules), .clock(clock), .out(out_force[23]),
    .reset(reset), .state(output_down[23]));
  \cell  cell_32 (
    .around({up[30], down[30], up[31], down[31], right_cells[0], right_cells[1], right_cells[2], output_down[30]}),
    .born_rule(born_rules), .survival_rule(survival_rules), .clock(clock), .out(out_force[31]),
    .reset(reset), .state(output_down[31]));

  assign output_up = output_down;

  // Other names for the same wires on the sheet: l2 = left_cells[2]; l1 = left_cells[1]; l0 = left_cells[0];
  //   d0 = down[0]; d1 = down[1]; d9 = down[9]; d17 = down[17]; d25 = down[25]; d2 = down[2]; d10 = down[10];
  //   d18 = down[18]; d26 = down[26]; m3 = output_down[3]; output[31:0] = output_down; d3 = down[3]; p3 = up[3];
  //   m11 = output_down[11]; d11 = down[11]; p11 = up[11]; m19 = output_down[19]; d19 = down[19]; p19 = up[19];
  //   m27 = output_down[27]; d27 = down[27]; p27 = up[27]; m4 = output_down[4]; d4 = down[4]; p4 = up[4];
  //   m12 = output_down[12]; d12 = down[12]; p12 = up[12]; m20 = output_down[20]; d20 = down[20]; p20 = up[20];
  //   m28 = output_down[28]; d28 = down[28]; p28 = up[28]; m7 = output_down[7]; m5 = output_down[5]; d5 = down[5];
  //   p5 = up[5]; m15 = output_down[15]; m13 = output_down[13]; d13 = down[13]; p13 = up[13]; m23 = output_down[23];
  //   m21 = output_down[21]; d21 = down[21]; p21 = up[21]; m31 = output_down[31]; m29 = output_down[29];
  //   d29 = down[29]; p29 = up[29]; m8 = output_down[8]; m6 = output_down[6]; d8 = down[8]; p8 = up[8]; d7 = down[7];
  //   p7 = up[7]; d6 = down[6]; p6 = up[6]; m16 = output_down[16]; m14 = output_down[14]; d16 = down[16];
  //   p16 = up[16]; d15 = down[15]; p15 = up[15]; d14 = down[14]; p14 = up[14]; m24 = output_down[24];
  //   m22 = output_down[22]; d24 = down[24]; p24 = up[24]; d23 = down[23]; p23 = up[23]; d22 = down[22]; p22 = up[22];
  //   m30 = output_down[30]; r2 = right_cells[2]; r1 = right_cells[1]; r0 = right_cells[0]; d31 = down[31];
  //   p31 = up[31]; d30 = down[30]; p30 = up[30]; bor[7:0] = born_rules; cl = clock; u0 = out_force[0];
  //   u1 = out_force[1]; u2 = out_force[2]; u3 = out_force[3]; u4 = out_force[4]; u5 = out_force[5];
  //   u6 = out_force[6]; u7 = out_force[7]; u8 = out_force[8]; u9 = out_force[9]; u10 = out_force[10];
  //   u11 = out_force[11]; u12 = out_force[12]; u13 = out_force[13]; u14 = out_force[14]; u15 = out_force[15];
  //   u16 = out_force[16]; u17 = out_force[17]; u18 = out_force[18]; u19 = out_force[19]; u20 = out_force[20];
  //   u21 = out_force[21]; u22 = out_force[22]; u23 = out_force[23]; u24 = out_force[24]; u25 = out_force[25];
  //   u26 = out_force[26]; u27 = out_force[27]; u28 = out_force[28]; u29 = out_force[29]; u30 = out_force[30];
  //   u31 = out_force[31]; m0 = output_down[0]; m1 = output_down[1]; m2 = output_down[2]; m9 = output_down[9];
  //   m10 = output_down[10]; m17 = output_down[17]; m18 = output_down[18]; m25 = output_down[25];
  //   m26 = output_down[26]; rs = reset; sur[7:0] = survival_rules; p0 = up[0]; p1 = up[1]; p2 = up[2]; p9 = up[9];
  //   p10 = up[10]; p17 = up[17]; p18 = up[18]; p25 = up[25]; p26 = up[26]
endmodule

module check_rules (
  input  [3:0] count,
  input  [7:0] born_rule,
  input  [7:0] survival_rule,
  output Born,
  output survive
);

  Multiplexer #(.select(4), .enable("false")) multiplexer_1 (
    .in0(1'b0), .in1(born_rule[0]), .in2(born_rule[1]), .in3(born_rule[2]), .in4(born_rule[3]),
    .in5(born_rule[4]), .in6(born_rule[5]), .in7(born_rule[6]), .in8(born_rule[7]), .out(Born), .sel(count));  // open: in9, in10, in11, in12, in13, in14, in15
  Multiplexer #(.select(4), .enable("false")) multiplexer_2 (
    .in0(1'b0), .in1(survival_rule[0]), .in2(survival_rule[1]), .in3(survival_rule[2]),
    .in4(survival_rule[3]), .in5(survival_rule[4]), .in6(survival_rule[5]), .in7(survival_rule[6]),
    .in8(survival_rule[7]), .out(survive), .sel(count));  // open: in9, in10, in11, in12, in13, in14, in15
endmodule
